// Logisim project 8 Bit Computer.circ as structural Verilog: 9 circuits, main circuit main
module main (
  input  PROGRAM,
  input  [7:0] ADDR,
  input  [7:0] DATA,
  input  RUN,
  output [7:0] BUS,
  output [7:0] out_6,
  output [7:0] out_7,
  output [7:0] out_8,
  output [3:0] OP,
  output [2:0] FLAGS,
  output [7:0] out_11,
  output [7:0] out_12,
  output [7:0] out_13,
  output [7:0] out_14,
  output [7:0] ADDR_2,
  output [7:0] out_16
);

  wire A_RD, A_WR, ADR_WR, ALU_BS, ALU_EN, ALU_OUT, and_1_out, B_RD, B_WR, CL_2_out, CL_3_out, CL_4_out,
       CL_5_out, CL_6_out, CL_out, clk_1_clk, CTR_RST, decoder_1_out0, decoder_1_out1, decoder_1_out2,
       decoder_1_out3, decoder_1_out4, decoder_1_out5, decoder_1_out6, decoder_1_out7, not_1_out, not_2_out,
       not_3_out, SET_out, STEP_out;
  wire [2:0] BRAIN_ctrl_ctr_out;
  wire [3:0] CLK_CTR;
  wire [7:0] controlled_buffer_1_out, controlled_buffer_3_out;
  wire [8:0] OUT_q;
  wire [23:0] rom_1_data;
  wire [31:5] CTRL;

  Button SET (.out(SET_out));
  LED ERROR (.in(CTRL[31]));
  LED HLT (.in(CLK_CTR[0]));
  LED PC_EN (.in(CLK_CTR[1]));
  LED JMP (.in(CLK_CTR[3]));
  LED u_CTR_RST (.in(CTR_RST));
  LED IR_WR (.in(CTRL[5]));
  LED PR_WR (.in(CTRL[8]));
  LED u_ADR_WR (.in(ADR_WR));
  LED RAM_EN (.in(CTRL[12]));
  LED RAM_RW (.in(CTRL[13]));
  Button STEP (.out(STEP_out));
  LED PC_OUT (.in(CLK_CTR[2]));
  LED led_1 (.in(decoder_1_out1));
  LED led_2 (.in(decoder_1_out2));
  LED led_3 (.in(decoder_1_out0));
  Decoder #(.select(3)) decoder_1 (
    .out0(decoder_1_out0), .out1(decoder_1_out1), .out2(decoder_1_out2), .out3(decoder_1_out3),
    .out4(decoder_1_out4), .out5(decoder_1_out5), .out6(decoder_1_out6), .out7(decoder_1_out7),
    .sel(BRAIN_ctrl_ctr_out), .en(1'b1));
  ctrl BRAIN (
    .CLK(and_1_out), .RST(CTR_RST), .REG_IR_IN(out_12), .CTRL_CTR_OUT(BRAIN_ctrl_ctr_out),
    .CTRL_DWORD({CTRL[31:26], ALU_BS, CTRL[24], OP, ALU_OUT, ALU_EN, B_RD, B_WR, A_RD, A_WR, CTRL[13:12], ADR_WR, CTRL[10:5], CTR_RST, CLK_CTR}),
    .REG_PR_IN(out_14), .FLAGS_IN(FLAGS));
  LED IR_CLR (.in(CTRL[7]));
  LED IR_RD (.in(CTRL[6]));
  LED PR_CLR (.in(CTRL[10]));
  LED PR_RD (.in(CTRL[9]));
  not not_1 (not_1_out, ADR_WR);
  Button CL (.out(CL_out));
  Button CL_2 (.out(CL_2_out));
  _7_Segment_Display u_7_segment_display_1 (
    .g(rom_1_data[8]), .f(rom_1_data[9]), .a(rom_1_data[10]), .b(rom_1_data[11]), .e(rom_1_data[15]),
    .d(rom_1_data[14]), .c(rom_1_data[13]), .dp(rom_1_data[12]));
  _7_Segment_Display u_7_segment_display_2 (
    .g(rom_1_data[16]), .f(rom_1_data[17]), .a(rom_1_data[18]), .b(rom_1_data[19]), .e(rom_1_data[23]),
    .d(rom_1_data[22]), .c(rom_1_data[21]), .dp(rom_1_data[20]));
  clk clk_1 (.HLT(CLK_CTR[0]), .CE(RUN), .STEP(STEP_out), .CLK(clk_1_clk));
  not not_2 (not_2_out, PROGRAM);
  prog_ctr PROG_CTR (
    .JMP(CLK_CTR[3]), .CE(CLK_CTR[1]), .CLK(and_1_out), .CLR(CL_3_out), .VALUE(out_6), .RE(CLK_CTR[2]),
    .BUS_OUT(BUS), .BUS_IN(BUS));
  Button CL_3 (.out(CL_3_out));
  LED led_4 (.in(decoder_1_out4));
  LED led_5 (.in(decoder_1_out6));
  LED led_6 (.in(decoder_1_out5));
  LED led_7 (.in(decoder_1_out3));
  Hex_Digit_Display hex_digit_display_1 (.value(out_12[7:4]));  // open: dp
  reg_irpr REG_IR (
    .WE(CTRL[5]), .CLK(and_1_out), .CLR(CTRL[7]), .VALUE(out_12), .RE(CTRL[6]), .BUS_OUT(BUS), .BUS_IN(BUS));
  reg_irpr REG_PR (
    .WE(CTRL[8]), .CLK(and_1_out), .CLR(CTRL[10]), .VALUE(out_14), .RE(CTRL[9]), .BUS_OUT(BUS), .BUS_IN(BUS));
  reg_gen REG_ADDR (
    .WE(ADR_WR), .CLK(and_1_out), .CLR(CL_out), .RE(not_1_out), .BUS_IN(BUS), .VALUE(ADDR_2));  // open: BUS_OUT
  assign controlled_buffer_1_out = not_3_out ? ADDR_2 : 8'bz;  // Controlled_Buffer controlled_buffer_1
  ram RAM (
    .ADDR(controlled_buffer_1_out), .CE(CTRL[12]), .CLK(and_1_out), .RW__1_RE__0_WE(CTRL[13]),
    .CLR(CL_2_out), .BUS_OUT(BUS), .BUS_IN(controlled_buffer_3_out), .PROG(PROGRAM), .SET(SET_out));
  assign controlled_buffer_1_out = PROGRAM ? ADDR : 8'bz;  // Controlled_Buffer controlled_buffer_2
  _7_Segment_Display u_7_segment_display_3 (
    .g(rom_1_data[0]), .f(rom_1_data[1]), .a(rom_1_data[2]), .b(rom_1_data[3]), .e(rom_1_data[7]),
    .d(rom_1_data[6]), .c(rom_1_data[5]), .dp(rom_1_data[4]));
  and and_1 (and_1_out, clk_1_clk, not_2_out);
  LED led_8 (.in(decoder_1_out7));
  Hex_Digit_Display hex_digit_display_2 (.value(out_12[3:0]));  // open: dp
  not not_3 (not_3_out, PROGRAM);
  assign controlled_buffer_3_out = not_3_out ? BUS : 8'bz;  // Controlled_Buffer controlled_buffer_3
  assign controlled_buffer_3_out = PROGRAM ? DATA : 8'bz;  // Controlled_Buffer controlled_buffer_4
  Button CL_4 (.out(CL_4_out));
  LED OUT_DSP (.in(CTRL[24]));
  LED u_ALU_EN (.in(ALU_EN));
  LED u_ALU_OUT (.in(ALU_OUT));
  reg_gen REG_A (.WE(A_WR), .CLK(and_1_out), .CLR(CL_5_out), .BUS_OUT(BUS), .RE(A_RD), .BUS_IN(BUS), .VALUE(out_13));
  Button CL_5 (.out(CL_5_out));
  reg_gen REG_B (.WE(B_WR), .CLK(and_1_out), .CLR(CL_6_out), .BUS_OUT(BUS), .RE(B_RD), .BUS_IN(BUS), .VALUE(out_16));
  Button CL_6 (.out(CL_6_out));
  Register #(.width(9)) OUT (.D({FLAGS[0], BUS}), .en(CTRL[24]), .Q(OUT_q), .clk(and_1_out), .clr(CL_4_out));
  alu ALU (
    .CE(ALU_EN), .A_IN(out_13), .BUS_IN(BUS), .OP_IN(OP), .CLK(and_1_out), .OUT0(out_7), .FLAGS_OUT(FLAGS),
    .OUT1(out_8));
  reg_alu reg_alu_1 (
    .CLK(and_1_out), .WE(ALU_EN), .RE(ALU_OUT), .BUS_OUT(BUS), .ALU_IN0(out_7), .ALU_IN1(out_8),
    .VALUE(out_11), .BS_IN(ALU_BS));
  LED u_ALU_BS (.in(ALU_BS));
  LED u_A_WR (.in(A_WR));
  LED u_A_RD (.in(A_RD));
  LED u_B_WR (.in(B_WR));
  LED u_B_RD (.in(B_RD));
  ROM #(.addrWidth(9), .dataWidth(24)) rom_1 (.addr(OUT_q), .data(rom_1_data));  // open: sel

  // Other names for the same wires on the sheet: CTRL (some bits) = {ALU_BS, OP, ALU_OUT, ALU_EN, B_RD, B_WR, A_RD, A_WR, ADR_WR, CTR_RST, CLK_CTR};
  //   IR_WR = CTRL[5]; IR_RD = CTRL[6]; IR_CLR = CTRL[7]; PR_WR = CTRL[8]; PR_RD = CTRL[9]; PR_CLR = CTRL[10];
  //   RAM_EN = CTRL[12]; RAM_RW = CTRL[13]; ALU_OP0 = OP[0]; ALU_OP1 = OP[1]; ALU_OP2 = OP[2]; ALU_OP3 = OP[3];
  //   OUT_DSP = CTRL[24]; UNUSED_26 = CTRL[26]; UNUSED_27 = CTRL[27]; UNUSED_28 = CTRL[28]; UNUSED_29 = CTRL[29];
  //   UNUSED_30 = CTRL[30]; ERROR = CTRL[31]

  // Notes on the sheet:
  //   RAM CONTROLS
  //   CLOCK CONTROL
  //   contents of rom_1 (hex, n*v repeats v):
  //   ee 28 cd 6d 2b 67 e7 2c ef 6f 28ee 2828 28cd 286d 282b 2867 28e7 282c 28ef 286f cdee cd28 cdcd cd6d
  //   cd2b cd67 cde7 cd2c cdef cd6f 6dee 6d28 6dcd 6d6d 6d2b 6d67 6de7 6d2c 6def 6d6f 2bee 2b28 2bcd 2b6d
  //   2b2b 2b67 2be7 2b2c 2bef 2b6f 67ee 6728 67cd 676d 672b 6767 67e7 672c 67ef 676f e7ee e728 e7cd e76d
  //   e72b e767 e7e7 e72c e7ef e76f 2cee 2c28 2ccd 2c6d 2c2b 2c67 2ce7 2c2c 2cef 2c6f efee ef28 efcd ef6d
  //   ef2b ef67 efe7 ef2c efef ef6f 6fee 6f28 6fcd 6f6d 6f2b 6f67 6fe7 6f2c 6fef 6f6f 28eeee 28ee28 28eecd
  //   28ee6d 28ee2b 28ee67 28eee7 28ee2c 28eeef 28ee6f 2828ee 282828 2828cd 28286d 28282b 282867 2828e7
  //   28282c 2828ef 28286f 28cdee 28cd28 28cdcd 28cd6d 28cd2b 28cd67 28cde7 28cd2c 28cdef 28cd6f 286dee
  //   286d28 286dcd 286d6d 286d2b 286d67 286de7 286d2c 286def 286d6f 282bee 282b28 282bcd 282b6d 282b2b
  //   282b67 282be7 282b2c 282bef 282b6f 2867ee 286728 2867cd 28676d 28672b 286767 2867e7 28672c 2867ef
  //   28676f 28e7ee 28e728 28e7cd 28e76d 28e72b 28e767 28e7e7 28e72c 28e7ef 28e76f 282cee 282c28 282ccd
  //   282c6d 282c2b 282c67 282ce7 282c2c 282cef 282c6f 28efee 28ef28 28efcd 28ef6d 28ef2b 28ef67 28efe7
  //   28ef2c 28efef 28ef6f 286fee 286f28 286fcd 286f6d 286f2b 286f67 286fe7 286f2c 286fef 286f6f cdeeee
  //   cdee28 cdeecd cdee6d cdee2b cdee67 cdeee7 cdee2c cdeeef cdee6f cd28ee cd2828 cd28cd cd286d cd282b
  //   cd2867 cd28e7 cd282c cd28ef cd286f cdcdee cdcd28 cdcdcd cdcd6d cdcd2b cdcd67 cdcde7 cdcd2c cdcdef
  //   cdcd6f cd6dee cd6d28 cd6dcd cd6d6d cd6d2b cd6d67 cd6de7 cd6d2c cd6def cd6d6f cd2bee cd2b28 cd2bcd
  //   cd2b6d cd2b2b cd2b67 cd2be7 cd2b2c cd2bef cd2b6f cd67ee cd6728 cd67cd cd676d cd672b cd6767 cd67e7
  //   cd672c cd67ef cd676f cde7ee cde728 cde7cd cde76d cde72b cde767 cde7e7 cde72c cde7ef cde76f cd2cee
  //   cd2c28 cd2ccd cd2c6d cd2c2b cd2c67 cd2ce7 cd2c2c cd2cef cd2c6f cdefee cdef28 cdefcd cdef6d cdef2b
  //   cdef67 cdefe7 cdef2c cdefef cdef6f cd6fee cd6f28 cd6fcd cd6f6d cd6f2b cd6f67 cd6fe7 cd6f2c cd6fef
  //   cd6f6f 6deeee 6dee28 6deecd 6dee6d 6dee2b 6dee67 6deee7 6dee2c 6deeef 6dee6f 6d28ee 6d2828 6d28cd
  //   6d286d 6d282b 6d2867 6d28e7 6d282c 6d28ef 6d286f 6dcdee 6dcd28 6dcdcd 6dcd6d 6dcd2b 6dcd67 6dcde7
  //   6dcd2c 6dcdef 6dcd6f 6d6dee 6d6d28 6d6dcd 6d6d6d 6d6d2b 6d6d67 6d6de7 6d6d2c 6d6def 6d6d6f 6d2bee
  //   6d2b28 6d2bcd 6d2b6d 6d2b2b 6d2b67 6d2be7 6d2b2c 6d2bef 6d2b6f 6d67ee 6d6728 6d67cd 6d676d 6d672b
  //   6d6767 6d67e7 6d672c 6d67ef 6d676f 6de7ee 6de728 6de7cd 6de76d 6de72b 6de767 6de7e7 6de72c 6de7ef
  //   6de76f 6d2cee 6d2c28 6d2ccd 6d2c6d 6d2c2b 6d2c67 6d2ce7 6d2c2c 6d2cef 6d2c6f 6defee 6def28 6defcd
  //   6def6d 6def2b 6def67 6defe7 6def2c 6defef 6def6f 6d6fee 6d6f28 6d6fcd 6d6f6d 6d6f2b 6d6f67 6d6fe7
  //   6d6f2c 6d6fef 6d6f6f 2beeee 2bee28 2beecd 2bee6d 2bee2b 2bee67 2beee7 2bee2c 2beeef 2bee6f 2b28ee
  //   2b2828 2b28cd 2b286d 2b282b 2b2867 2b28e7 2b282c 2b28ef 2b286f 2bcdee 2bcd28 2bcdcd 2bcd6d 2bcd2b
  //   2bcd67 2bcde7 2bcd2c 2bcdef 2bcd6f 2b6dee 2b6d28 2b6dcd 2b6d6d 2b6d2b 2b6d67 2b6de7 2b6d2c 2b6def
  //   2b6d6f 2b2bee 2b2b28 2b2bcd 2b2b6d 2b2b2b 2b2b67 2b2be7 2b2b2c 2b2bef 2b2b6f 2b67ee 2b6728 2b67cd
  //   2b676d 2b672b 2b6767 2b67e7 2b672c 2b67ef 2b676f 2be7ee 2be728 2be7cd 2be76d 2be72b 2be767 2be7e7
  //   2be72c 2be7ef 2be76f 2b2cee 2b2c28 2b2ccd 2b2c6d 2b2c2b 2b2c67 2b2ce7 2b2c2c 2b2cef 2b2c6f 2befee
  //   2bef28 2befcd 2bef6d 2bef2b 2bef67 2befe7 2bef2c 2befef 2bef6f 2b6fee 2b6f28 2b6fcd 2b6f6d 2b6f2b
  //   2b6f67 2b6fe7 2b6f2c 2b6fef 2b6f6f 67eeee 67ee28 67eecd 67ee6d 67ee2b 67ee67 67eee7 67ee2c 67eeef
  //   67ee6f 6728ee 672828
endmodule

module clk (
  input  HLT,
  input  CE,
  input  STEP,
  output CLK
);

  wire and_1_out, and_2_out, clock_1_out, controlled_inverter_1_out, not_1_out, not_2_out, or_1_out;

  Clock clock_1 (.out(clock_1_out));
  and and_1 (and_1_out, clock_1_out, CE);
  not not_1 (not_1_out, CE);
  and and_2 (and_2_out, not_1_out, STEP);
  or or_1 (or_1_out, and_1_out, and_2_out);
  assign controlled_inverter_1_out = not_2_out ? ~HLT : 1'bz;  // Controlled_Inverter controlled_inverter_1
  not not_2 (not_2_out, STEP);
  assign controlled_inverter_1_out = STEP ? STEP : 1'bz;  // Controlled_Buffer controlled_buffer_1
  and and_3 (CLK, controlled_inverter_1_out, or_1_out);
endmodule

module ctrl (
  input  CLK,
  input  RST,
  input  [7:0] REG_IR_IN,
  input  [7:0] REG_PR_IN,
  input  [2:0] FLAGS_IN,
  output [2:0] CTRL_CTR_OUT,
  output [31:0] CTRL_DWORD
);

  wire not_1_out;
  wire [2:0] controlled_buffer_1_out;

  assign controlled_buffer_1_out = RST ? 3'b000 : 3'bz;  // Controlled_Buffer controlled_buffer_1
  Counter #(.width(3), .max('h7)) counter_1 (
    .load(RST), .D(controlled_buffer_1_out), .count(not_1_out), .Q(CTRL_CTR_OUT), .clk(CLK));  // open: carry, clr
  not not_1 (not_1_out, RST);
  ROM #(.addrWidth(16), .dataWidth(32)) rom_1 (
    .addr({REG_IR_IN, FLAGS_IN, REG_PR_IN[1:0], CTRL_CTR_OUT}), .data(CTRL_DWORD), .sel(1'b1));

  // Notes on the sheet:
  //   contents of rom_1 (hex, n*v repeats v):
  //   804 3022 490 5*0 804 3022 490 5*0 804 3022 490 5*0 804 3022 490 5*0 804 3022 490 5*0 804 3022 490
  //   5*0 804 3022 490 5*0 804 3022 490 5*0 804 3022 490 5*0 804 3022 490 5*0 804 3022 490 5*0 804 3022
  //   490 5*0 804 3022 490 5*0 804 3022 490 5*0 804 3022 490 5*0 804 3022 490 5*0 804 3022 490 5*0 804
  //   3022 490 5*0 804 3022 490 5*0 804 3022 490 5*0 804 3022 490 5*0 804 3022 490 5*0 804 3022 490 5*0
  //   804 3022 490 5*0 804 3022 490 5*0 804 3022 490 5*0 804 3022 490 5*0 804 3022 490 5*0 804 3022 490
  //   5*0 804 3022 490 5*0 804 3022 490 5*0 804 3022 490 5*0 804 3022 806 3100 80000001 490 0 0 804 3022
  //   806 3100 24490 490 0 0 804 3022 806 3100 18490 490 0 0 804 3022 806 3100 80000001 490 0 0 804 3022
  //   806 3100 80000001 490 0 0 804 3022 806 3100 18000 490 0 0 804 3022 806 3100 24000 490 0 0 804 3022
  //   806 3100 80000001 490 0 0 804 3022 806 3100 80000001 490 0 0 804 3022 806 3100 18000 490 0 0 804
  //   3022 806 3100 24000 490 0 0 804 3022 806 3100 80000001 490 0 0 804 3022 806 3100 80000001 490 0 0
  //   804 3022 806 3100 18000 490 0 0 804 3022 806 3100 24000 490 0 0 804 3022 806 3100 80000001 490 0 0
  //   804 3022 806 3100 80000001 490 0 0 804 3022 806 3100 18000 490 0 0 804 3022 806 3100 24000 490 0 0
  //   804 3022 806 3100 80000001 490 0 0 804 3022 806 3100 80000001 490 0 0 804 3022 806 3100 18000 490 0
  //   0 804 3022 806 3100 24000 490 0 0 804 3022 806 3100 80000001 490 0 0 804 3022 806 3100 80000001 490
  //   0 0 804 3022 806 3100 18000 490 0 0 804 3022 806 3100 24000 490 0 0 804 3022 806 3100 80000001 490 0
  //   0 804 3022 806 3100 80000001 490 0 0 804 3022 806 3100 18000 490 0 0 804 3022 806 3100 24000 490 0 0
  //   804 3022 806 3100 80000001 490 0 0 804 3022 806 7490 4*0 804 3022 806 7490 4*0 804 3022 806 7490 4*0
  //   804 3022 806 7490 4*0 804 3022 806 7490 4*0 804 3022 806 7490 4*0 804 3022 806 7490 4*0 804 3022 806
  //   7490 4*0 804 3022 806 7490 4*0 804 3022 806 7490 4*0 804 3022 806 7490 4*0 804 3022 806 7490 4*0 804
  //   3022 806 7490 4*0 804 3022 806 7490 4*0 804 3022 806 7490 4*0 804 3022 806 7490 4*0 804 3022 806
  //   7490 4*0 804 3022 806 7490 4*0 804 3022 806 7490 4*0 804 3022 806 7490 4*0 804 3022 806 7490 4*0 804
  //   3022 806 7490 4*0 804 3022 806 7490 4*0 804 3022 806 7490 4*0 804 3022 806 7490 4*0 804 3022 806
  //   7490 4*0 804 3022 806 7490 4*0 804 3022 806 7490 4*0 804 3022 806 7490 4*0 804 3022 806 7490 4*0 804
  //   3022 806 7490 4*0 804 3022 806 7490 4*0 804 3022 806 13490 4*0 804 3022 806 13490 4*0 804 3022 806
  //   13490 4*0 804 3022 806 13490 4*0 804 3022 806 13490 4*0 804 3022 806 13490 4*0 804 3022 806 13490
  //   4*0 804 3022 806 13490 4*0 804 3022 806 13490 4*0 804 3022 806 13490 4*0 804 3022 806 13490 4*0 804
  //   3022 806 13490 4*0 804 3022 806 13490 4*0 804 3022 806 13490 4*0 804 3022 806 13490 4*0 804 3022 806
  //   13490 4*0 804 3022 806 13490 4*0 804 3022 806 13490 4*0 804 3022 806 13490 4*0 804 3022 806 13490
  //   4*0 804 3022 806 13490 4*0 804 3022 806 13490 4*0 804 3022 806 13490 4*0 804 3022 806 13490 4*0 804
  //   3022 806 13490 4*0 804 3022 806 13490 4*0 804 3022 806 13490 4*0 804 3022 806 13490 4*0 804 3022 806
  //   13490 4*0 804 3022 806 13490 4*0 804 3022 806 13490 4*0 804 3022 806 13490 4*0 804 3022 806 3800
  //   7000 c94 0 0 804 3022 806 3800 7000 c94 0 10 804 3022 806 3800 7000 c94 0 10 804 3022 806 3800 7000
  //   c94 0 10 804 3022 806 3800 7000 c94 0 10 804 3022 806 3800 7000 c94 0 10 804 3022 806 3800 7000 c94
  //   0 10 804 3022 806 3800 7000 c94 0 10 804 3022 806 3800 7000 c94 0 10 804 3022 806 3800 7000 c94 0 10
  //   804 3022 806 3800 7000 c94 0 10 804 3022 806 3800 7000 c94 0 10 804 3022 806 3800 7000 c94 0 10 804
  //   3022 806 3800 7000 c94 0 10 804 3022 806 3800 7000 c94 0 10 804 3022 806 3800 7000 c94 0 10 804 3022
  //   806 3800 7000 c94 0 10 804 3022 806 3800 7000 c94 0 10 804 3022 806 3800 7000 c94 0 10 804 3022 806
  //   3800 7000 c94 0 10 804 3022 806 3800 7000 c94 0 10 804 3022 806 3800 7000 c94 0 10 804 3022 806 3800
  //   7000 c94 0 10 804 3022 806 3800 7000 c94 0 10 804 3022 806 3800 7000 c94 0 10 804 3022 806 3800 7000
  //   c94 0 10 804 3022 806 3800 7000 c94 0 10 804 3022 806 3800 7000 c94 0 10 804 3022 806 3800 7000 c94
  //   0 10 804 3022 806 3800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
endmodule

module reg_irpr (
  input  WE,
  input  CLR,
  input  CLK,
  input  RE,
  input  [7:0] BUS_IN,
  output [7:0] VALUE,
  output [7:0] BUS_OUT
);

  wire or_1_out;
  wire [7:0] controlled_buffer_1_out;

  assign controlled_buffer_1_out = CLR ? {8{1'b0}} : 8'bz;  // Controlled_Buffer controlled_buffer_1
  or or_1 (or_1_out, WE, CLR);
  assign controlled_buffer_1_out = WE ? BUS_IN : 8'bz;  // Controlled_Buffer controlled_buffer_2
  Register register_1 (.D(controlled_buffer_1_out), .en(or_1_out), .Q(VALUE), .clk(CLK));  // open: clr
  assign BUS_OUT = RE ? VALUE : 8'bz;  // Controlled_Buffer controlled_buffer_3
endmodule

module reg_gen (
  input  WE,
  input  CLK,
  input  CLR,
  input  RE,
  input  [7:0] BUS_IN,
  output [7:0] VALUE,
  output [7:0] BUS_OUT
);

  wire [7:0] controlled_buffer_1_out;

  assign controlled_buffer_1_out = WE ? BUS_IN : 8'bz;  // Controlled_Buffer controlled_buffer_1
  Register register_1 (.D(controlled_buffer_1_out), .en(WE), .Q(VALUE), .clk(CLK), .clr(CLR));
  assign BUS_OUT = RE ? VALUE : 8'bz;  // Controlled_Buffer controlled_buffer_2
endmodule

module reg_alu (
  input  [7:0] ALU_IN0,
  input  CLK,
  input  [7:0] ALU_IN1,
  input  WE,
  input  RE,
  input  BS_IN,
  output [7:0] VALUE,
  output [7:0] BUS_OUT
);

  wire not_1_out;
  wire [7:0] controlled_buffer_2_out, controlled_buffer_4_out, register_1_q, register_2_q;

  assign BUS_OUT = RE ? VALUE : 8'bz;  // Controlled_Buffer controlled_buffer_1
  assign controlled_buffer_2_out = WE ? ALU_IN0 : 8'bz;  // Controlled_Buffer controlled_buffer_2
  Register register_1 (.D(controlled_buffer_2_out), .en(WE), .Q(register_1_q), .clk(CLK));  // open: clr
  assign VALUE = not_1_out ? register_1_q : 8'bz;  // Controlled_Buffer controlled_buffer_3
  not not_1 (not_1_out, BS_IN);
  assign controlled_buffer_4_out = WE ? ALU_IN1 : 8'bz;  // Controlled_Buffer controlled_buffer_4
  Register register_2 (.D(controlled_buffer_4_out), .en(WE), .Q(register_2_q), .clk(CLK));  // open: clr
  assign VALUE = BS_IN ? register_2_q : 8'bz;  // Controlled_Buffer controlled_buffer_5
endmodule

module ram (
  input  [7:0] ADDR,
  input  [7:0] BUS_IN,
  input  CLR,
  input  CE,
  input  PROG,
  input  RW__1_RE__0_WE,
  input  CLK,
  input  SET,
  output [7:0] BUS_OUT
);

  wire and_1_out, and_2_out, and_3_out, nand_1_out, not_1_out, or_1_out, or_2_out;
  wire [7:0] ram_1_data;

  or or_1 (or_1_out, CE, PROG);
  nand nand_1 (nand_1_out, PROG, RW__1_RE__0_WE);
  or or_2 (or_2_out, CLK, SET);
  and and_1 (and_1_out, nand_1_out, RW__1_RE__0_WE);
  RAM ram_1 (.addr(ADDR), .data(ram_1_data), .sel(or_1_out), .clk(or_2_out), .ld(and_1_out), .clr(CLR));
  and and_2 (and_2_out, or_1_out, and_1_out);
  not not_1 (not_1_out, and_1_out);
  assign BUS_OUT = and_2_out ? ram_1_data : 8'bz;  // Controlled_Buffer controlled_buffer_1
  assign ram_1_data = and_3_out ? BUS_IN : 8'bz;  // Controlled_Buffer controlled_buffer_2
  and and_3 (and_3_out, or_1_out, not_1_out);
endmodule

module alu (
  input  CE,
  input  [7:0] A_IN,
  input  [7:0] BUS_IN,
  input  [3:0] OP_IN,
  input  CLK,
  output [7:0] OUT0,
  output [2:0] FLAGS_OUT,
  output [7:0] OUT1
);

  wire adder_1_cout, and_2_out, decoder_1_out0, decoder_1_out1, decoder_1_out2, decoder_1_out3,
       decoder_1_out4, decoder_1_out5, decoder_1_out6, nor_1_out, nor_2_out, subtractor_1_bout;
  wire [2:0] controlled_buffer_2_out;
  wire [7:0] adder_1_out, adder_2_out, and_1_out, controlled_buffer_5_out, multiplier_1_cout,
       multiplier_1_out, or_1_out, subtractor_1_out, subtractor_2_out;

  Decoder #(.select(4)) decoder_1 (
    .out0(decoder_1_out0), .out1(decoder_1_out1), .out2(decoder_1_out2), .out3(decoder_1_out3),
    .out4(decoder_1_out4), .out5(decoder_1_out5), .out6(decoder_1_out6), .sel(OP_IN));  // open: out7, out8, out9, out10, out11, out12, out13, out14, out15, en
  assign controlled_buffer_2_out[2] = decoder_1_out0 ? 1'b0 : 1'bz;  // Controlled_Buffer controlled_buffer_1
  assign controlled_buffer_2_out[0] = decoder_1_out1 ? 1'b0 : 1'bz;  // Controlled_Buffer controlled_buffer_2
  assign controlled_buffer_2_out[2] = decoder_1_out2 ? 1'b0 : 1'bz;  // Controlled_Buffer controlled_buffer_3
  assign controlled_buffer_2_out[2] = decoder_1_out3 ? 1'b0 : 1'bz;  // Controlled_Buffer controlled_buffer_4
  Adder adder_1 (.a(A_IN), .b(BUS_IN), .out(adder_1_out), .cin(1'b0), .cout(adder_1_cout));
  assign controlled_buffer_5_out = decoder_1_out0 ? adder_1_out : 8'bz;  // Controlled_Buffer controlled_buffer_5
  assign controlled_buffer_2_out[0] = decoder_1_out0 ? adder_1_cout : 1'bz;  // Controlled_Buffer controlled_buffer_6
  assign controlled_buffer_5_out = decoder_1_out1 ? subtractor_1_out : 8'bz;  // Controlled_Buffer controlled_buffer_7
  Subtractor subtractor_1 (.a(A_IN), .b(BUS_IN), .out(subtractor_1_out), .bin(1'b0), .bout(subtractor_1_bout));
  assign controlled_buffer_2_out[2] = decoder_1_out1 ? subtractor_1_bout : 1'bz;  // Controlled_Buffer controlled_buffer_8
  assign controlled_buffer_5_out = decoder_1_out2 ? and_1_out : 8'bz;  // Controlled_Buffer controlled_buffer_9
  assign and_1_out = BUS_IN & BUS_IN;  // AND_Gate and_1, 8 bits wide
  assign controlled_buffer_5_out = decoder_1_out3 ? or_1_out : 8'bz;  // Controlled_Buffer controlled_buffer_10
  assign or_1_out = A_IN | BUS_IN;  // OR_Gate or_1, 8 bits wide
  Adder adder_2 (.a(BUS_IN), .b(8'h1), .out(adder_2_out), .cin(1'b0));  // open: cout
  Subtractor subtractor_2 (.a(BUS_IN), .b(8'h1), .out(subtractor_2_out), .bin(1'b0));  // open: bout
  Multiplier multiplier_1 (.a(A_IN), .b(BUS_IN), .out(multiplier_1_out), .cout(multiplier_1_cout));  // open: cin
  assign controlled_buffer_2_out[2] = decoder_1_out6 ? 1'b0 : 1'bz;  // Controlled_Buffer controlled_buffer_11
  assign controlled_buffer_2_out[0] = decoder_1_out2 ? 1'b0 : 1'bz;  // Controlled_Buffer controlled_buffer_12
  assign controlled_buffer_2_out[0] = decoder_1_out3 ? 1'b0 : 1'bz;  // Controlled_Buffer controlled_buffer_13
  assign controlled_buffer_5_out = decoder_1_out4 ? adder_2_out : 8'bz;  // Controlled_Buffer controlled_buffer_14
  assign controlled_buffer_5_out = decoder_1_out5 ? subtractor_2_out : 8'bz;  // Controlled_Buffer controlled_buffer_15
  assign controlled_buffer_5_out = decoder_1_out6 ? multiplier_1_out : 8'bz;  // Controlled_Buffer controlled_buffer_16
  assign OUT1 = decoder_1_out6 ? multiplier_1_cout : 8'bz;  // Controlled_Buffer controlled_buffer_17
  assign OUT0 = CE ? controlled_buffer_5_out : 8'bz;  // Controlled_Buffer controlled_buffer_18
  assign controlled_buffer_2_out[0] = decoder_1_out6 ? ~nor_2_out : 1'bz;  // Controlled_Inverter controlled_inverter_1
  Register #(.width(3)) register_1 (.D(controlled_buffer_2_out), .en(CE), .Q(FLAGS_OUT), .clk(CLK));  // open: clr
  assign controlled_buffer_2_out[1] = CE ? and_2_out : 1'bz;  // Controlled_Buffer controlled_buffer_19
  nor nor_1 (nor_1_out, controlled_buffer_5_out[0], controlled_buffer_5_out[1], controlled_buffer_5_out[2], controlled_buffer_5_out[3], controlled_buffer_5_out[4], controlled_buffer_5_out[5], controlled_buffer_5_out[6], controlled_buffer_5_out[7]);
  nor nor_2 (nor_2_out, OUT1[0], OUT1[1], OUT1[2], OUT1[3], OUT1[4], OUT1[5], OUT1[6], OUT1[7]);
  and and_2 (and_2_out, nor_1_out, nor_2_out);

  // Notes on the sheet:
  //   EF ZF CF
  //   2   1   0 
  //   0:ADD | 1:SUB | 2:AND | 3:OR | 4:INC | 5:DEC | 6:MUL | 7:AND | 8:AND | 9:AND | A:AND | B:AND | C:AND | D:AND | E:AND | F:AND
endmodule

module prog_ctr (
  input  JMP,
  input  CE,
  input  CLK,
  input  CLR,
  input  RE,
  input  [7:0] BUS_IN,
  output [7:0] VALUE,
  output [7:0] BUS_OUT
);

  wire [7:0] controlled_buffer_1_out;

  assign controlled_buffer_1_out = JMP ? BUS_IN : 8'bz;  // Controlled_Buffer controlled_buffer_1
  Counter counter_1 (
    .load(JMP), .D(controlled_buffer_1_out), .count(CE), .Q(VALUE), .clk(CLK), .clr(CLR));  // open: carry
  assign BUS_OUT = RE ? VALUE : 8'bz;  // Controlled_Buffer controlled_buffer_2
endmodule
